// Logisim project P2.circ as structural Verilog
module main (
);

  wire alu_1_p3, clock_1_out, multiplexer_2_out, registerfile_1_p1, registerfile_1_p2, registerfile_1_p3;
  wire [31:0] adder_1_out, adder_2_out, bit_extender_1_out, multiplexer_1_out, PC_q, risc_vprogramrom_1_p2;

  Register #(.width(32)) PC (.D(multiplexer_1_out), .clk(clock_1_out), .Q(PC_q));  // open: en, clr
  Multiplexer #(.width(32), .enable("false")) multiplexer_1 (
    .in0(adder_1_out), .in1(adder_2_out), .out(multiplexer_1_out));  // open: sel
  Clock clock_1 (.out(clock_1_out));
  Register register_1 ();  // open: D, en, Q, clk, clr
  Adder #(.width(32)) adder_1 (.a(PC_q), .b(32'h4), .out(adder_1_out));  // open: cin, cout
  // RISC_VProgramROM risc_vprogramrom_1: pin names not known; wires that end beside it: PC_q, risc_vprogramrom_1_p2
  // Incrementer incrementer_1: pin names not known
  assign bit_extender_1_out = {{31{risc_vprogramrom_1_p2[31]}}, risc_vprogramrom_1_p2[31]};  // Bit_Extender bit_extender_1
  Adder #(.width(32)) adder_2 (.a(PC_q), .b(bit_extender_1_out), .out(adder_2_out));  // open: cin, cout
  // RegisterFile registerfile_1: pin names not known; wires that end beside it: registerfile_1_p1, registerfile_1_p2, registerfile_1_p3
  Multiplexer #(.enable("false")) multiplexer_2 (
    .in0(registerfile_1_p3), .in1(risc_vprogramrom_1_p2[31]), .out(multiplexer_2_out));  // open: sel
  // ALU alu_1: pin names not known; wires that end beside it: registerfile_1_p2, multiplexer_2_out, alu_1_p3, alu_1_p3
  RAM ram_1 ();  // open: addr, data, sel, clk, ld, clr
  Multiplexer #(.enable("false")) multiplexer_3 (.in1(alu_1_p3), .out(registerfile_1_p1));  // open: in0, sel
endmodule
